# Fritzing sketch Arduino (saved by Fritzing 0.9.0b)
breadboards: 1

parts:
  Part1 = Arduino Uno (Rev3)
  R1 = Resistor [tolerance=±5% resistance=220 package=THT]
  R2 = Photocell (LDR) [package=THT]
  RHT1 = Humidity and Temperature Sensor RHT03
  J1 = Basic Force Sensing Resistor (FSR) [package=THT]
  R3 = Resistor [tolerance=±5% resistance=220 package=THT]
  S1 = Reed switch [package=THT]
  MIC2 = Microphone

nets (from the breadboard view):
  N1: Part1.A0, MIC2.pin2
  N2: Part1.A1, RHT1.Data-signal
  N3: Part1.A2, R1.Pin_0, R2.pin_1
  3V3: Part1.3V3, Part1.5V, R2.pin_0, RHT1.Vcc, J1.pin_0, S1.pin_1
  N4: Part1.GND, R1.Pin_1, RHT1.GND_1, R3.Pin_1, S1.pin_2, MIC2.pin1
  N5: J1.pin_1, R3.Pin_0
